# Fritzing sketch LED Segment Display (saved by Fritzing 0.9.3b)
breadboards: 1

parts:
  U1 = 74HC595 [package="DIP16 [THT]"]
  DI1 = 7-Segment LED Display [package=THT]
  Mod1 = Raspberry Pi Pico
  R1 = Resistor [tolerance=±5% resistance=220 package=THT]

nets:
  N1: U1.Q1, DI1.cathodeB
  N2: U1.Q2, DI1.cathodeC
  N3: U1.Q3, DI1.cathodeD
  N4: U1.Q4, DI1.cathodeE
  N5: U1.Q5, DI1.cathodeF
  N6: U1.Q6, DI1.cathodeG
  N7: U1.Q7, DI1.cathodeDP
  N8: U1.GND, U1.OE, Mod1.pin_3, Mod1.pin_8, Mod1.pin_13, Mod1.pin_18, Mod1.pin_23, Mod1.pin_28, Mod1.pin_33, Mod1.pin_38, Mod1.pin_42, Mod1.pin_45, Mod1.pin_46, Mod1.pin_55, Mod1.pin_56, Mod1.pin_65, Mod1.pin_66, Mod1.pin_75, Mod1.pin_76, Mod1.pin_85, Mod1.pin_86, Mod1.pin_95, Mod1.pin_96, Mod1.pin_105, Mod1.pin_106, Mod1.pin_115, Mod1.pin_116, R1.Pin_1
  N9: U1.MR, U1.VCC, Mod1.pin_36, Mod1.pin_49, Mod1.pin_50
  N10: U1.SH_CP, Mod1.pin_4, Mod1.pin_113, Mod1.pin_114
  N11: U1.ST_CP, Mod1.pin_2, Mod1.pin_117, Mod1.pin_118
  N12: U1.DS, Mod1.pin_1, Mod1.pin_119, Mod1.pin_120
  N13: U1.Q0, DI1.cathodeA
  N14: DI1.commAnode#2, R1.Pin_0
  N15: Mod1.pin_5, Mod1.pin_111, Mod1.pin_112
  N16: Mod1.pin_6, Mod1.pin_109, Mod1.pin_110
  N17: Mod1.pin_7, Mod1.pin_107, Mod1.pin_108
  N18: Mod1.pin_9, Mod1.pin_103, Mod1.pin_104
  N19: Mod1.pin_10, Mod1.pin_101, Mod1.pin_102
  N20: Mod1.pin_11, Mod1.pin_99, Mod1.pin_100
  N21: Mod1.pin_12, Mod1.pin_97, Mod1.pin_98
  N22: Mod1.pin_14, Mod1.pin_93, Mod1.pin_94
  N23: Mod1.pin_15, Mod1.pin_91, Mod1.pin_92
  N24: Mod1.pin_16, Mod1.pin_89, Mod1.pin_90
  N25: Mod1.pin_17, Mod1.pin_87, Mod1.pin_88
  N26: Mod1.pin_19, Mod1.pin_83, Mod1.pin_84
  N27: Mod1.pin_20, Mod1.pin_81, Mod1.pin_82
  N28: Mod1.pin_21, Mod1.pin_79, Mod1.pin_80
  N29: Mod1.pin_22, Mod1.pin_77, Mod1.pin_78
  N30: Mod1.pin_24, Mod1.pin_73, Mod1.pin_74
  N31: Mod1.pin_25, Mod1.pin_71, Mod1.pin_72
  N32: Mod1.pin_26, Mod1.pin_69, Mod1.pin_70
  N33: Mod1.pin_27, Mod1.pin_67, Mod1.pin_68
  N34: Mod1.pin_29, Mod1.pin_63, Mod1.pin_64
  N35: Mod1.pin_30, Mod1.pin_61, Mod1.pin_62
  N36: Mod1.pin_31, Mod1.pin_59, Mod1.pin_60
  N37: Mod1.pin_32, Mod1.pin_57, Mod1.pin_58
  N38: Mod1.pin_34, Mod1.pin_53, Mod1.pin_54
  N39: Mod1.pin_35, Mod1.pin_51, Mod1.pin_52
  N40: Mod1.pin_37, Mod1.pin_47, Mod1.pin_48
  N41: Mod1.pin_39, Mod1.pin_44

custom parts:
  Raspberry Pi Pico: Raspberry Pi Pico. Based around the RP2040 microcontroller the Pico is a low cost microcontroller device bringing Raspberry Pi quality, cost, and easy of use to the microcontroller space. Jan 2021, Split part in to two versions: tht (this one) and SMD. This one will drill holes for a .1 in header in pcb to allow plugging in the module as well as providing pads to solder the module to the top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
